# Fritzing sketch aquaman-client-board (saved by Fritzing 0.9.3b)
breadboards: 1

parts:
  nodeMCU = NodeMCU V1.0
  4_Channel_Relay1 = 4 Channel Power Relay
  S1 = SWITCH-MOMENTARY-2 [package=tactile-pth]
  S2 = SWITCH-MOMENTARY-2 [package=tactile-pth]
  S3 = SWITCH-MOMENTARY-2 [package=tactile-pth]
  LED1 = LED - 5mm [color="Green (555nm)" package="5 mm [THT]"]
  LED2 = LED - 5mm [color="Blue (470nm)" package="5 mm [THT]"]
  LED3 = LED - 5mm [color="Red (635nm)" package="5 mm [THT]"]
  R4 = Resistor [tolerance=±5% resistance=10k package=THT]
  R5 = Resistor [tolerance=±5% resistance=10k package=THT]
  R6 = Resistor [tolerance=±5% resistance=10k package=THT]
  V1 = DC Power [voltage=5V]

nets:
  N1: nodeMCU.D0, 4_Channel_Relay1.IN1
  N2: nodeMCU.D1, 4_Channel_Relay1.IN2
  N3: nodeMCU.D2, 4_Channel_Relay1.IN3
  N4: nodeMCU.D3, S1.1
  N5: nodeMCU.D4, S2.1
  3V3: nodeMCU.3V3, 4_Channel_Relay1.VCC
  GND: nodeMCU.GND, 4_Channel_Relay1.GND, S1.2, S2.2, S3.2, V1.V-
  N6: nodeMCU.D5, S3.1
  N7: nodeMCU.D6, LED1.anode
  N8: nodeMCU.D7, LED2.anode
  N9: nodeMCU.D8, LED3.anode
  N10: nodeMCU.Vin, V1.V+
  N11: LED1.cathode, R4.Pin_0
  N12: LED2.cathode, R5.Pin_0
  N13: LED3.cathode, R6.Pin_0
  N14: R4.Pin_1, R5.Pin_1, R6.Pin_1

custom parts:
  NodeMCU V1.0: ESP8266 based NodeMCU
  4 Channel Power Relay: A 4 channel power relay. The module operates at 5V.
